# Fritzing sketch fan_controller (saved by Fritzing 0.9.2b)
breadboards: 1

parts:
  IC2 = PICAXE-18M [package=THT]
  U5 = mystery part, 3 pins [chip_label=DC-to-DC]
  C3 = Ceramic Capacitor [capacitance=10µF package="200 mil [THT, multilayer]"]
  C4 = Ceramic Capacitor [capacitance=10µF package="200 mil [THT, multilayer]"]
  Fan = SWITCH-MOMENTARY-2 [package=reed_switch_plastic]
  Lights = SWITCH-MOMENTARY-2 [package=reed_switch_plastic]
  UseSensors = SWITCH-MOMENTARY-2 [package=reed_switch_plastic]
  R15 = Rotary Potentiometer (Small) [maximum_resistance=100kΩ package=THT]
  R16 = PHOTOCELL [package=photocell]
  R17 = Resistor [tolerance=±5% resistance=10k package=THT]
  R18 = Resistor [tolerance=±5% resistance=10k package=THT]
  R19 = Resistor [tolerance=±5% resistance=10k package=THT]
  Q5 = Basic FET N-Channel [package="TO220 [THT]"]
  D8 = Zener Diode [part_number=1N4732A breakdown_voltage=3.6V package="Melf DO-213 AB [SMD]"]
  Q6 = Basic FET N-Channel [package="TO220 [THT]"]
  D10 = Rectifier Diode [part_number=1N4001 package="Melf DO-213 AB [SMD]"]
  LED4 = LED - 5mm [color="White (8000K)" current=20 package="5 mm [THT]"]
  R22 = Resistor [tolerance=±5% resistance=100k package=THT]
  J4 = male pin header, 4 pins [form="♂ (male)"]
  R23 = Resistor [tolerance=±5% resistance=10k package=THT]
  12v1 = Power plug
  J5 = male pin header, 4 pins [form="♂ (male)"]
  R24 = Resistor [tolerance=±5% resistance=47 package=THT]
  D11 = Rectifier Diode [part_number=1N4001 package="Melf DO-213 AB [SMD]"]
  R25 = Resistor [tolerance=±5% resistance=100 package=THT]
  LED5 = LED - 5mm [color="White (8000K)" current=20 package="5 mm [THT]"]
  LED6 = LED - 5mm [color="White (8000K)" current=20 package="5 mm [THT]"]

nets:
  N1: IC2.Serial_Out, J4.pin1
  N2: IC2.Serial_In, R22.Pin_0, J4.pin2
  N3: IC2.Reset, J4.pin3
  N4: IC2.0V, U5.pin2, C3.1, C4.0, R17.Pin_0, R18.Pin_0, R19.Pin_0, Q5.source, Q6.source, R22.Pin_1, J4.pin4, R23.Pin_0, 12v1.GND, R24.Pin_0
  N5: IC2.Out_2, Q5.gate
  N6: IC2.Out_3, J5.pin4
  N7: IC2.Out_4, Q6.gate, R25.Pin_1
  N8: IC2.Out_7, Fan.1, R19.Pin_1
  N9: IC2.+V, U5.pin3, C4.1, Fan.2, Lights.2, UseSensors.2, R15.leg2, R16.P$2
  N10: IC2.In_6_/_Keyboard_Clock, Lights.1, R18.Pin_1
  N11: IC2.In_7_/_Keyboard_Data, UseSensors.1, R17.Pin_1
  N12: IC2.In_0_/_ADC_0_/_Infrain, R15.wiper
  N13: IC2.In_1_/_ADC_1, R16.P$1, R23.Pin_1
  N14: U5.pin1, C3.0, D10.cathode, 12v1.VCC, J5.pin2, D11.cathode, LED5.anode
  N15: R15.leg1, R24.Pin_1
  N16: Q5.drain, D8.cathode, D10.anode, J5.pin1
  N17: Q6.drain, D11.anode
  N18: LED4.cathode, LED6.anode
  N19: LED4.anode, LED5.cathode
  N20: R25.Pin_0, LED6.cathode
